// Digital circuit 1-16 BIT DUPLICATOR.dig as structural Verilog
module _1_16_BIT_DUPLICATOR (
  input  IN,
  output [15:0] OUT
);

  _1_8_BIT_DUPLICATOR _1_8_bit_duplicator_1 (.IN(IN), .OUT(OUT[7:0]));
  _1_8_BIT_DUPLICATOR _1_8_bit_duplicator_2 (.IN(IN), .OUT(OUT[15:8]));
endmodule

/* Test case:
IN	OUT
0	0
1	0xFFFF
*/
