// Digital circuit 1-32 BIT DUPLICATOR.dig as structural Verilog
module _1_32_BIT_DUPLICATOR (
  input  IN,
  output [31:0] OUT
);

  _1_16_BIT_DUPLICATOR _1_16_bit_duplicator_1 (.IN(IN), .OUT(OUT[15:0]));
  _1_16_BIT_DUPLICATOR _1_16_bit_duplicator_2 (.IN(IN), .OUT(OUT[31:16]));
endmodule

/* Test case:
IN	OUT
0	0
1	0xFFFFFFFF
*/
