// Digital circuit 1-8 BIT DUPLICATOR.dig as structural Verilog
module _1_8_BIT_DUPLICATOR (
  input  IN,
  output [7:0] OUT
);


  assign OUT = {8{IN}};
endmodule

/* Test case:
IN	OUT
0	0
1	0xFF
*/
