// Digital circuit 16-BIT INVERT.dig as structural Verilog
module _16_BIT_INVERT (
  input  [15:0] IN,
  input  INVERT,
  output [15:0] OUT
);

  _8_BIT_INVERT _8_bit_invert_1 (.IN(IN[7:0]), .INVERT(INVERT), .OUT(OUT[7:0]));
  _8_BIT_INVERT _8_bit_invert_2 (.IN(IN[15:8]), .INVERT(INVERT), .OUT(OUT[15:8]));
endmodule

/* Test case:
IN      INVERT  OUT
0       0       0
0       1       0xFFFF
0xFFFF  0       0xFFFF
0xFFFF  1       0
0x00FF  1       0xFF00
0x1234  1       0xEDCB
0xA5A5  0       0xA5A5
loop(i,16)
(1<<i)  0       (1<<i)
(1<<i)  1       (0xFFFF-(1<<i))
end loop
*/
