// Digital circuit 32-BIT INVERT.dig as structural Verilog
module _32_BIT_INVERT (
  input  [31:0] IN,
  input  INVERT,
  output [31:0] OUT
);

  _16_BIT_INVERT _16_bit_invert_1 (.IN(IN[15:0]), .INVERT(INVERT), .OUT(OUT[15:0]));
  _16_BIT_INVERT _16_bit_invert_2 (.IN(IN[31:16]), .INVERT(INVERT), .OUT(OUT[31:16]));
endmodule

/* Test case:
IN          INVERT  OUT
0           0       0
0           1       0xFFFFFFFF
0xFFFFFFFF  0       0xFFFFFFFF
0xFFFFFFFF  1       0
0x0000FFFF  1       0xFFFF0000
0x12345678  1       0xEDCBA987
0xA5A5A5A5  0       0xA5A5A5A5
loop(i,32)
(1<<i)      0       (1<<i)
(1<<i)      1       (0xFFFFFFFF-(1<<i))
end loop
*/
