// Digital circuit 4 TO 1 NOR.dig as structural Verilog
module _4_TO_1_NOR (
  input  [3:0] IN,
  output OUT
);

  wire [1:0] or_1_out;

  assign or_1_out = IN[1:0] | IN[3:2];  // Or or_1, 2 bits wide
  nor nor_1 (OUT, or_1_out[0], or_1_out[1]);
endmodule

/* Test case:
IN		OUT
0		1
loop(i,4)	
(i+1)		0
end loop
*/
