// Digital circuit 4 TO 1 OR.dig as structural Verilog
module _4_TO_1_OR (
  input  [3:0] IN,
  output OUT
);

  wire [1:0] or_1_out;

  assign or_1_out = IN[1:0] | IN[3:2];  // Or or_1, 2 bits wide
  or or_2 (OUT, or_1_out[0], or_1_out[1]);
endmodule

/* Test case:
IN		OUT
0		0
loop(i,14)
(i+1)		1
end loop
*/
