// Digital circuit 4-BIT INVERT.dig as structural Verilog
module _4_BIT_INVERT (
  input  [3:0] IN,
  input  INVERT,
  output [3:0] OUT
);

  xor xor_1 (OUT[0], IN[0], INVERT);
  xor xor_2 (OUT[1], IN[1], INVERT);
  xor xor_3 (OUT[2], IN[2], INVERT);
  xor xor_4 (OUT[3], IN[3], INVERT);
endmodule

/* Test case:
IN   INVERT  OUT
0    0       0
0    1       0xF
0xF  0       0xF
0xF  1       0
0x5  1       0xA
0xA  1       0x5
0x1  1       0xE
0x8  1       0x7
loop(i,16)
(i)  0       (i)
(i)  1       (15-i)
end loop
*/
