// Digital circuit 4-BIT LOOKAHEAD ADDER.dig as structural Verilog
module _4_BIT_LOOKAHEAD_ADDER (
  input  [3:0] A,
  input  [3:0] B,
  input  C0,
  output COUT,
  output [3:0] OUT
);

  wire and_1_out, and_2_out, and_3_out, and_4_out, and_5_out, and_6_out, and_7_out, and_8_out, and_9_out,
       and_10_out, or_1_out, or_2_out, or_3_out, or_4_out, or_5_out, or_6_out, or_7_out, or_8_out, or_9_out,
       or_10_out, PG0_g, PG0_p, PG1_g, PG1_p, PG2_g, PG2_p, PG3_g, PG3_p;

  PG_CHIP PG3 (.A(B[3]), .B(A[3]), .G(PG3_g), .P(PG3_p));
  PG_CHIP PG2 (.A(A[2]), .B(B[2]), .G(PG2_g), .P(PG2_p));
  PG_CHIP PG1 (.A(A[1]), .B(B[1]), .G(PG1_g), .P(PG1_p));
  PG_CHIP PG0 (.A(B[0]), .B(A[0]), .G(PG0_g), .P(PG0_p));
  and and_1 (and_1_out, PG0_g, PG1_p);
  and and_2 (and_2_out, PG0_p, C0);
  and and_3 (and_3_out, PG2_g, PG3_p);
  and and_4 (and_4_out, PG1_g, PG2_p);
  and and_5 (and_5_out, PG1_p, and_2_out);
  or or_1 (or_1_out, and_2_out, PG0_g);
  or or_2 (or_2_out, PG3_g, and_3_out);
  and and_6 (and_6_out, and_4_out, PG3_p);
  and and_7 (and_7_out, and_1_out, PG2_p);
  and and_8 (and_8_out, PG2_p, and_5_out);
  and and_9 (and_9_out, PG3_p, and_7_out);
  and and_10 (and_10_out, PG3_p, and_8_out);
  or or_3 (or_3_out, or_2_out, and_6_out);
  xor xor_1 (OUT[0], PG0_p, C0);
  or or_4 (or_4_out, and_4_out, PG2_g);
  or or_5 (or_5_out, and_5_out, and_1_out);
  or or_6 (or_6_out, PG1_g, or_5_out);
  or or_7 (or_7_out, and_7_out, or_4_out);
  or or_8 (or_8_out, and_8_out, or_7_out);
  xor xor_2 (OUT[1], or_1_out, PG1_p);
  or or_9 (or_9_out, and_9_out, and_10_out);
  xor xor_3 (OUT[3], or_8_out, PG3_p);
  xor xor_4 (OUT[2], or_6_out, PG2_p);
  or or_10 (or_10_out, and_6_out, or_9_out);
  or or_11 (COUT, or_3_out, or_10_out);

  // Notes on the sheet:
  //   P1*G0
  //   P0*C0
  //   P3*G2
  //   P2*G1
  //   P1*P0*C0
  //   C1
  //   P3*P2*G1
  //   P2*P1*G0
  //   P2*P1*P0*C0
  //   P3*P2*P1*G0
  //   P3*P2*P1*P0*C0
  //   0
  //   C2
  //   C3
  //   1
  //   3
  //   2
  //   C4
endmodule

/* Test case:
A  B  C0  OUT  COUT
0  0  0   0    0
0  0  1   1    0
5  1  0   6    0
5  3  0   8    0
7  1  0   8    0
9  6  0   15   0
9  6  1   0    1
15 1  0   0    1
15 0  1   0    1
8  8  0   0    1
6  6  1   13   0
12 7  0   3    1
15 15 0   14   1
15 15 1   15   1
*/
