// Digital circuit 64 AND 1.dig as structural Verilog
module _64_AND_1 (
  input  [63:0] A,
  input  B,
  output [63:0] OUT
);

  assign OUT = A & {64{B}};  // And and_1, 64 bits wide
endmodule

/* Test case:
A                   B  OUT
0                   0  0
0                   1  0
0xFFFFFFFFFFFFFFFF  0  0
0xFFFFFFFFFFFFFFFF  1  0xFFFFFFFFFFFFFFFF
0x0123456789ABCDEF  1  0x0123456789ABCDEF
0x0123456789ABCDEF  0  0
0xA5A5A5A5A5A5A5A5  1  0xA5A5A5A5A5A5A5A5
0x5A5A5A5A5A5A5A5A  1  0x5A5A5A5A5A5A5A5A
0x8000000000000000  1  0x8000000000000000
0x8000000000000000  0  0
0x0000000000000001  1  0x0000000000000001
0x0000000000000001  0  0
0x00000000FFFFFFFF  1  0x00000000FFFFFFFF
0xFFFFFFFF00000000  1  0xFFFFFFFF00000000
loop(i,64)
(1<<i)              1  (1<<i)
(1<<i)              0  0
end loop
*/
