// Digital circuit 64 TO 1 NOR.dig as structural Verilog
module _64_TO_1_NOR (
  input  [63:0] A,
  output OUT
);

  wire [1:0] or_5_out;
  wire [3:0] or_4_out;
  wire [7:0] or_3_out;
  wire [15:0] or_2_out;
  wire [31:0] or_1_out;

  assign or_1_out = A[31:0] | A[63:32];  // Or or_1, 32 bits wide
  assign or_2_out = or_1_out[15:0] | or_1_out[31:16];  // Or or_2, 16 bits wide
  assign or_3_out = or_2_out[7:0] | or_2_out[15:8];  // Or or_3, 8 bits wide
  assign or_4_out = or_3_out[3:0] | or_3_out[7:4];  // Or or_4, 4 bits wide
  assign or_5_out = or_4_out[1:0] | or_4_out[3:2];  // Or or_5, 2 bits wide
  nor nor_1 (OUT, or_5_out[0], or_5_out[1]);
endmodule

/* Test case:
A                   OUT
0                   1
1                   0
0x8000000000000000  0
0xFFFFFFFFFFFFFFFF  0
0x00000000FFFFFFFF  0
0xFFFFFFFF00000000  0
0x0000000000000080  0
0x0000000000000100  0
0x0000000000008000  0
0x0000000000010000  0
0x0000000080000000  0
0x0000000100000000  0
0x00FF000000000000  0
0x0101010101010101  0
0xA5A5A5A5A5A5A5A5  0
0x5A5A5A5A5A5A5A5A  0
loop(i,64)
(1<<i)              0
end loop
*/
