// Digital circuit 64-1 BIT NOR.dig as structural Verilog
module _64_1_BIT_NOR (
  input  [63:0] A,
  input  [63:0] B,
  output OUT
);

  wire or_9_out, or_10_out, or_11_out, or_12_out, or_13_out, or_14_out;
  wire [7:0] or_2_out, or_3_out, or_4_out, or_5_out, or_6_out, or_7_out, or_8_out;
  wire [63:0] or_1_out;

  assign or_1_out = A | B;  // Or or_1, 64 bits wide
  assign or_2_out = or_1_out[7:0] | or_1_out[15:8];  // Or or_2, 8 bits wide
  assign or_3_out = or_1_out[23:16] | or_1_out[31:24];  // Or or_3, 8 bits wide
  assign or_4_out = or_1_out[39:32] | or_1_out[47:40];  // Or or_4, 8 bits wide
  assign or_5_out = or_1_out[55:48] | or_1_out[63:56];  // Or or_5, 8 bits wide
  assign or_6_out = or_2_out | or_3_out;  // Or or_6, 8 bits wide
  assign or_7_out = or_4_out | or_5_out;  // Or or_7, 8 bits wide
  assign or_8_out = or_6_out | or_7_out;  // Or or_8, 8 bits wide
  or or_9 (or_9_out, or_8_out[0], or_8_out[1]);
  or or_10 (or_10_out, or_8_out[2], or_8_out[3]);
  or or_11 (or_11_out, or_8_out[4], or_8_out[5]);
  or or_12 (or_12_out, or_8_out[6], or_8_out[7]);
  or or_13 (or_13_out, or_9_out, or_10_out);
  or or_14 (or_14_out, or_11_out, or_12_out);
  nor nor_1 (OUT, or_13_out, or_14_out);
endmodule

/* Test case:
A                   B  OUT
0                   0  1
1                   0  0
0x80                0  0
0x100               0  0
0x8000              0  0
0x10000             0  0
0x80000000          0  0
0x100000000         0  0
0x8000000000000000  0  0
0xFFFFFFFFFFFFFFFF  0  0
0x00000000FFFFFFFF  0  0
0xFFFFFFFF00000000  0  0
0x0101010101010101  0  0
*/
