// Digital circuit 64-BIT ALU.dig as structural Verilog
module _64_BIT_ALU (
  input  [63:0] A,
  input  [63:0] B,
  input  SUB,
  output [63:0] OUT,
  output COUT
);

  wire [63:0] _64_bit_invert_1_out;

  _64_BIT_INVERT _64_bit_invert_1 (.IN(B), .INVERT(SUB), .OUT(_64_bit_invert_1_out));
  Add #(.Bits(64)) add_1 (.a(A), .b(_64_bit_invert_1_out), .c_i(SUB), .s(OUT), .c_o(COUT));
endmodule

/* Test case:
A                   B                   SUB  OUT                 COUT
0                   0                   0    0                   0
7                   5                   0    12                  0
7                   5                   1    2                   1
5                   5                   1    0                   1
5                   7                   1    0xFFFFFFFFFFFFFFFE  0
0                   1                   1    0xFFFFFFFFFFFFFFFF  0
0                   0                   1    0                   1
100                 123                 1    0xFFFFFFFFFFFFFFE9  0
1000000             2345678             0    3345678             0
0xFFFFFFFF          1                   0    0x100000000         0
0xFFFFFFFFFFFFFFFF  1                   0    0                   1
0x7FFFFFFFFFFFFFFF  1                   0    0x8000000000000000  0
0x8000000000000000  0x8000000000000000  0    0                   1
0xFFFFFFFFFFFFFFFF  0xFFFFFFFFFFFFFFFF  0    0xFFFFFFFFFFFFFFFE  1
0x123456789ABCDEF0  0x0FEDCBA987654321  0    0x2222222222222211  0
*/
