// Digital circuit 64-BIT INVERT.dig as structural Verilog
module _64_BIT_INVERT (
  input  [63:0] IN,
  input  INVERT,
  output [63:0] OUT
);

  _32_BIT_INVERT _32_bit_invert_1 (.IN(IN[31:0]), .INVERT(INVERT), .OUT(OUT[31:0]));
  _32_BIT_INVERT _32_bit_invert_2 (.IN(IN[63:32]), .INVERT(INVERT), .OUT(OUT[63:32]));
endmodule

/* Test case:
IN                  INVERT  OUT
0                   0       0
0                   1       0xFFFFFFFFFFFFFFFF
0xFFFFFFFFFFFFFFFF  0       0xFFFFFFFFFFFFFFFF
0xFFFFFFFFFFFFFFFF  1       0
0x00000000FFFFFFFF  1       0xFFFFFFFF00000000
0x0123456789ABCDEF  1       0xFEDCBA9876543210
0xA5A5A5A5A5A5A5A5  0       0xA5A5A5A5A5A5A5A5
0x8000000000000000  1       0x7FFFFFFFFFFFFFFF
0x0000000000000001  1       0xFFFFFFFFFFFFFFFE
loop(i,64)
(1<<i)              0       (1<<i)
(1<<i)              1       (0xFFFFFFFFFFFFFFFF-(1<<i))
end loop
*/
