// Digital circuit 8-BIT INVERT.dig as structural Verilog
module _8_BIT_INVERT (
  input  [7:0] IN,
  input  INVERT,
  output [7:0] OUT
);

  _4_BIT_INVERT _4_bit_invert_1 (.IN(IN[3:0]), .INVERT(INVERT), .OUT(OUT[3:0]));
  _4_BIT_INVERT _4_bit_invert_2 (.IN(IN[7:4]), .INVERT(INVERT), .OUT(OUT[7:4]));
endmodule

/* Test case:
IN    INVERT  OUT
0     0       0
0     1       0xFF
0xFF  0       0xFF
0xFF  1       0
0x0F  1       0xF0
0xA5  1       0x5A
0x5A  0       0x5A
0x80  1       0x7F
0x01  1       0xFE
loop(i,256)
(i)   0       (i)
(i)   1       (255-i)
end loop
*/
