// Digital circuit ALU.dig as structural Verilog
module ALU (
  input  [63:0] A,
  input  [63:0] B,
  input  [3:0] OP,
  output C,
  output [63:0] OUT,
  output Z,
  output N,
  output V
);

  wire decoder_1_out_1, xor_2_out, xor_3_out;
  wire [62:0] _64_bit_alu_1_out;
  wire [63:0] and_1_out, or_1_out, SAR_out, SHL_out, SHR_out, xor_1_out;

  Decoder #(.Selector_Bits(4)) decoder_1 (
    .sel(OP), .out_1(decoder_1_out_1));  // open: out_0, out_2, out_3, out_4, out_5, out_6, out_7, out_8, out_9, out_10, out_11, out_12, out_13, out_14, out_15
  BarrelShifter #(.Bits(64)) SHL (.in(A), .shift({1'b0, B[5:0]}), .out(SHL_out));
  BarrelShifter #(.Bits(64), .direction("right")) SHR (.in(A), .shift({1'b0, B[5:0]}), .out(SHR_out));
  BarrelShifter #(.barrelShifterMode("arithmetic"), .Bits(64), .direction("right")) SAR (
    .in(A), .shift({1'b0, B[5:0]}), .out(SAR_out));
  _64_BIT_ALU _64_bit_alu_1 (.A(A), .B(B), .SUB(decoder_1_out_1), .OUT({N, _64_bit_alu_1_out}), .C(C));
  assign and_1_out = A & B;  // And and_1, 64 bits wide
  assign or_1_out = A | B;  // Or or_1, 64 bits wide
  assign xor_1_out = A ^ B;  // XOr xor_1, 64 bits wide
  xor xor_2 (xor_2_out, B[63], A[63]);
  xor xor_3 (xor_3_out, A[63], N);
  Multiplexer #(.Selector_Bits(4), .Bits(64)) multiplexer_1 (
    .sel(OP), .in_0({N, _64_bit_alu_1_out}), .in_1({N, _64_bit_alu_1_out}), .in_2(and_1_out),
    .in_3(or_1_out), .in_4(xor_1_out), .in_5(SHL_out), .in_6(SHR_out), .in_7(SAR_out), .in_8(B),
    .in_9({64{1'b0}}), .in_10({64{1'b0}}), .in_11({64{1'b0}}), .in_12({64{1'b0}}), .in_13({64{1'b0}}),
    .in_14({64{1'b0}}), .in_15({64{1'b0}}), .out(OUT));
  _64_TO_1_NOR _64_to_1_nor_1 (.A({N, _64_bit_alu_1_out}), .OUT(Z));
  and and_2 (V, xor_2_out, xor_3_out);
endmodule

/* Test case:
A                   B                   OP  OUT              Z  N  C  V

0x0000000000000005  0x0000000000000003  0   0x0000000000000008  X  X  X  X
0x0000000000000000  0x0000000000000000  0   0x0000000000000000  X  X  X  X
0xFFFFFFFFFFFFFFFF  0x0000000000000001  0   0x0000000000000000  X  X  X  X
0x7FFFFFFFFFFFFFFF  0x0000000000000001  0   0x8000000000000000  X  X  X  X
0x123456789ABCDEF0  0x0FEDCBA987654321  0   0x2222222222222211  X  X  X  X

0x0000000000000005  0x0000000000000003  1   0x0000000000000002  0  0  1  0
0x0000000000000003  0x0000000000000005  1   0xFFFFFFFFFFFFFFFE  0  1  0  0
0x0000000000000005  0x0000000000000005  1   0x0000000000000000  1  0  1  0
0x0000000000000000  0x0000000000000001  1   0xFFFFFFFFFFFFFFFF  0  1  0  0
0xFFFFFFFFFFFFFFFD  0xFFFFFFFFFFFFFFFB  1   0x0000000000000002  0  0  1  0
0xFFFFFFFFFFFFFFFB  0xFFFFFFFFFFFFFFFD  1   0xFFFFFFFFFFFFFFFE  0  1  0  0
0xFFFFFFFFFFFFFFFF  0x0000000000000001  1   0xFFFFFFFFFFFFFFFE  0  1  1  0
0x0000000000000001  0xFFFFFFFFFFFFFFFF  1   0x0000000000000002  0  0  0  0
0x7FFFFFFFFFFFFFFF  0xFFFFFFFFFFFFFFFF  1   0x8000000000000000  0  1  0  1
0x8000000000000000  0x0000000000000001  1   0x7FFFFFFFFFFFFFFF  0  0  1  1
0x8000000000000000  0x8000000000000000  1   0x0000000000000000  1  0  1  0

0xFF00FF00FF00FF00  0x0FF00FF00FF00FF0  2   0x0F000F000F000F00  X  X  X  X
0xFFFFFFFFFFFFFFFF  0x0000000000000000  2   0x0000000000000000  X  X  X  X
0xFFFFFFFFFFFFFFFF  0xFFFFFFFFFFFFFFFF  2   0xFFFFFFFFFFFFFFFF  X  X  X  X

0xFF00FF00FF00FF00  0x0FF00FF00FF00FF0  3   0xFFF0FFF0FFF0FFF0  X  X  X  X
0x0000000000000000  0x0000000000000000  3   0x0000000000000000  X  X  X  X
0x8000000000000000  0x0000000000000001  3   0x8000000000000001  X  X  X  X

0xFF00FF00FF00FF00  0x0FF00FF00FF00FF0  4   0xF0F0F0F0F0F0F0F0  X  X  X  X
0xFFFFFFFFFFFFFFFF  0xFFFFFFFFFFFFFFFF  4   0x0000000000000000  X  X  X  X
0xA5A5A5A5A5A5A5A5  0xFFFFFFFFFFFFFFFF  4   0x5A5A5A5A5A5A5A5A  X  X  X  X

0x0000000000000001  0x0000000000000000  5   0x0000000000000001  X  X  X  X
0x0000000000000001  0x0000000000000001  5   0x0000000000000002  X  X  X  X
0x0000000000000001  0x000000000000003F  5   0x8000000000000000  X  X  X  X
0x0123456789ABCDEF  0x0000000000000004  5   0x123456789ABCDEF0  X  X  X  X
0x0000000000000001  0x0000000000000041  5   0x0000000000000002  X  X  X  X
0xFFFFFFFFFFFFFFFF  0x0000000000000020  5   0xFFFFFFFF00000000  X  X  X  X

0x8000000000000000  0x0000000000000001  6   0x4000000000000000  X  X  X  X
0x8000000000000000  0x000000000000003F  6   0x0000000000000001  X  X  X  X
0x0123456789ABCDEF  0x0000000000000004  6   0x00123456789ABCDE  X  X  X  X
0xFFFFFFFFFFFFFFFF  0x0000000000000000  6   0xFFFFFFFFFFFFFFFF  X  X  X  X

0x8000000000000000  0x0000000000000001  7   0xC000000000000000  X  X  X  X
0x8000000000000000  0x000000000000003F  7   0xFFFFFFFFFFFFFFFF  X  X  X  X
0xFFFFFFFFFFFFFFF0  0x0000000000000002  7   0xFFFFFFFFFFFFFFFC  X  X  X  X
0x4000000000000000  0x0000000000000001  7   0x2000000000000000  X  X  X  X
0x0123456789ABCDEF  0x0000000000000004  7   0x00123456789ABCDE  X  X  X  X

0x1111111111111111  0x2222222222222222  8   0x2222222222222222  X  X  X  X
0xFFFFFFFFFFFFFFFF  0x0000000000000000  8   0x0000000000000000  X  X  X  X
*/
