// Digital circuit CALC.dig as structural Verilog
module CALC (
  input  [63:0] A,
  input  [63:0] B,
  input  [1:0] OP,
  input  EQ,
  input  RESET,
  input  CLK,
  output [63:0] OUT
);

  // CPU cpu_1: pin names not known; wires that end beside it: CLK, RESET, A, B, {{62{1'b0}}, OP}, {{63{1'b0}}, EQ}, OUT
  // Probe on OUT

  // Notes on the sheet:
  //   CLK: Hz: 100000
endmodule
