// Digital circuit CONDITION UNIT.dig as structural Verilog
module CONDITION_UNIT (
  input  C,
  input  N,
  input  V,
  input  Z,
  input  [2:0] COND,
  input  BRANCH,
  output JUMP
);

  wire multiplexer_1_out, not_1_out, not_2_out, not_3_out, xor_1_out;

  xor xor_1 (xor_1_out, N, V);
  not not_1 (not_1_out, Z);
  not not_2 (not_2_out, xor_1_out);
  not not_3 (not_3_out, C);
  Multiplexer #(.Selector_Bits(3)) multiplexer_1 (
    .sel(COND), .in_0(1'b1), .in_1(Z), .in_2(not_1_out), .in_3(xor_1_out), .in_4(not_2_out),
    .in_5(not_3_out), .in_6(C), .in_7(1'b0), .out(multiplexer_1_out));
  and and_1 (JUMP, BRANCH, multiplexer_1_out);
endmodule

/* Test case:
Z  N  C  V  COND  BRANCH  JUMP

0  0  0  0  0     1       1
1  1  1  1  0     1       1
1  0  0  0  0     1       1
0  1  0  0  0     1       1
0  0  1  0  0     1       1
0  0  0  1  0     1       1
0  1  1  1  0     1       1
1  1  0  0  0     1       1
0  1  0  1  0     1       1
1  0  1  1  0     1       1

0  0  0  0  1     1       0
1  1  1  1  1     1       1
1  0  0  0  1     1       1
0  1  0  0  1     1       0
0  0  1  0  1     1       0
0  0  0  1  1     1       0
0  1  1  1  1     1       0
1  1  0  0  1     1       1
0  1  0  1  1     1       0
1  0  1  1  1     1       1

0  0  0  0  2     1       1
1  1  1  1  2     1       0
1  0  0  0  2     1       0
0  1  0  0  2     1       1
0  0  1  0  2     1       1
0  0  0  1  2     1       1
0  1  1  1  2     1       1
1  1  0  0  2     1       0
0  1  0  1  2     1       1
1  0  1  1  2     1       0

0  0  0  0  3     1       0
1  1  1  1  3     1       0
1  0  0  0  3     1       0
0  1  0  0  3     1       1
0  0  1  0  3     1       0
0  0  0  1  3     1       1
0  1  1  1  3     1       0
1  1  0  0  3     1       1
0  1  0  1  3     1       0
1  0  1  1  3     1       1

0  0  0  0  4     1       1
1  1  1  1  4     1       1
1  0  0  0  4     1       1
0  1  0  0  4     1       0
0  0  1  0  4     1       1
0  0  0  1  4     1       0
0  1  1  1  4     1       1
1  1  0  0  4     1       0
0  1  0  1  4     1       1
1  0  1  1  4     1       0

0  0  0  0  5     1       1
1  1  1  1  5     1       0
1  0  0  0  5     1       1
0  1  0  0  5     1       1
0  0  1  0  5     1       0
0  0  0  1  5     1       1
0  1  1  1  5     1       0
1  1  0  0  5     1       1
0  1  0  1  5     1       1
1  0  1  1  5     1       0

0  0  0  0  6     1       0
1  1  1  1  6     1       1
1  0  0  0  6     1       0
0  1  0  0  6     1       0
0  0  1  0  6     1       1
0  0  0  1  6     1       0
0  1  1  1  6     1       1
1  1  0  0  6     1       0
0  1  0  1  6     1       0
1  0  1  1  6     1       1

0  0  0  0  7     1       0
1  1  1  1  7     1       0
1  0  0  0  7     1       0
0  1  0  0  7     1       0
0  0  1  0  7     1       0
0  0  0  1  7     1       0
0  1  1  1  7     1       0
1  1  0  0  7     1       0
0  1  0  1  7     1       0
1  0  1  1  7     1       0

1  1  1  1  0     0       0
0  0  0  0  0     0       0
1  1  1  1  1     0       0
0  0  0  0  1     0       0
1  1  1  1  2     0       0
0  0  0  0  2     0       0
1  1  1  1  3     0       0
0  0  0  0  3     0       0
1  1  1  1  4     0       0
0  0  0  0  4     0       0
1  1  1  1  5     0       0
0  0  0  0  5     0       0
1  1  1  1  6     0       0
0  0  0  0  6     0       0
1  1  1  1  7     0       0
0  0  0  0  7     0       0
*/
