// Digital circuit CPU.dig as structural Verilog
module CPU (
  input  CLK,
  input  RESET,
  input  [63:0] X_IN,
  input  [63:0] M_IN,
  output [15:0] M_ADDR,
  output [63:0] M_OUT,
  output [63:0] M_WR
);

  wire and_1_out, not_1_out, not_2_out, or_1_out;
  wire [11:8] undriven;
  wire [31:0] IR_q, MICROCODE_d;
  wire [63:32] IR_q_2;

  not not_1 (not_1_out, MICROCODE_d[15]);
  or or_1 (or_1_out, not_1_out, RESET);
  and and_1 (and_1_out, CLK, or_1_out);
  not not_2 (not_2_out, and_1_out);
  CounterPreset #(.Bits(8)) PC (.C(not_2_out));  // open: en, dir, in, ld, clr, out, ovf
  Register #(.Bits(64)) IR (.en(and_1_out), .Q({IR_q_2, IR_q}));  // open: D, C
  Driver #(.Bits(64)) driver_1 (.in({32'h1, IR_q}));  // open: en, out
  ROM #(.AddrBits(12), .Bits(32)) MICROCODE (.A({undriven, IR_q_2[63:56]}), .sel(1'b1), .D(MICROCODE_d));
  Register #(.Bits(64)) A ();  // open: D, C, en, Q
  Register #(.Bits(64)) B ();  // open: D, C, en, Q
  // Pins of 8 and 12 bits meet at {undriven, IR_q_2[63:56]}

  // Notes on the sheet:
  //   CLK: Hz: 100000
  //   contents of MICROCODE (hex, n*v repeats v):
  //   30100,400,15*0,405,15*0,40a,15*0,484,15*0,11,c24,14*0,11,c64,14*0
  //   ,600,15*0,1400,15*0,2400,15*0,100400,15*0,90,c24,14*0,90,c64,14*0
  //   ,200404,15*0,4040a,15*0,40405,15*0,8000,15*0,80408
endmodule
