// Digital circuit CPU_000.dig as structural Verilog
module CPU_000 (
  input  RESET,
  input  [63:0] MIN,
  input  CLK,
  output MWR,
  output [7:0] MBE,
  output [63:0] MOUT,
  output [31:0] DBGPC,
  output [31:0] MADDR
);

  wire _4_to_1_or_1_out, alu_1_c, alu_1_n, alu_1_v, alu_1_z, and_1_out, condition_unit_1_jump, not_1_out,
       not_2_out, or_1_out, or_2_out, or_3_out, register_1_q, register_2_q, register_3_q, register_4_q;
  wire [1:0] MICROCODE_d_2, MICROCODE_d_3, MICROCODE_d_6;
  wire [2:0] MICROCODE_d_5;
  wire [3:0] counter_1_out, MICROCODE_d_4, multiplexer_7_out;
  wire [7:0] _1_8_bit_duplicator_1_out, and_2_out;
  wire [31:0] add_1_s, alu_1_out, MICROCODE_d, multiplexer_1_out, multiplexer_2_out, multiplexer_3_out,
       reg_file_1_d_a;
  wire [63:0] imm_1_out, IR_q, load_formatter_1_out, multiplexer_4_out, multiplexer_6_out, reg_file_1_d_b;
  wire [63:32] alu_1_out_2, reg_file_1_d_a_2;

  not not_1 (not_1_out, MICROCODE_d[25]);
  or or_1 (or_1_out, not_1_out, RESET);
  and and_1 (and_1_out, CLK, or_1_out);
  Multiplexer #(.Bits(32)) multiplexer_1 (
    .sel(MICROCODE_d[20]), .in_0(IR_q[31:0]), .in_1(reg_file_1_d_a), .out(multiplexer_1_out));
  Multiplexer #(.Bits(32)) multiplexer_2 (
    .sel(condition_unit_1_jump), .in_0(add_1_s), .in_1(multiplexer_1_out), .out(multiplexer_2_out));
  or or_2 (or_2_out, RESET, MICROCODE_d[1]);
  not not_2 (not_2_out, and_1_out);
  Multiplexer #(.Bits(32)) multiplexer_3 (
    .sel(RESET), .in_0(multiplexer_2_out), .in_1({32{1'b0}}), .out(multiplexer_3_out));
  or or_3 (or_3_out, or_2_out, condition_unit_1_jump);
  Register #(.Bits(32)) PC (.D(multiplexer_3_out), .C(not_2_out), .en(or_3_out), .Q(DBGPC));
  LOAD_FORMATTER load_formatter_1 (
    .M_IN(MIN), .LANE(MADDR[2:0]), .M_SIZE(MICROCODE_d_6), .M_SIGNED(MICROCODE_d[23]),
    .OUT(load_formatter_1_out));
  Add #(.Bits(32)) add_1 (.a(DBGPC), .b(32'h8), .c_i(1'b0), .s(add_1_s));  // open: c_o
  Multiplexer #(.Selector_Bits(2), .Bits(64)) multiplexer_4 (
    .sel(MICROCODE_d_2), .in_0({alu_1_out_2, alu_1_out}), .in_1(load_formatter_1_out),
    .in_2({{32{1'b0}}, DBGPC}), .in_3({64{1'b0}}), .out(multiplexer_4_out));
  Register #(.Bits(64)) IR (.D(MIN), .C(and_1_out), .en(MICROCODE_d[0]), .Q(IR_q));
  Multiplexer #(.Bits(32)) multiplexer_5 (.sel(MICROCODE_d[2]), .in_0(DBGPC), .in_1(alu_1_out), .out(MADDR));
  IMM imm_1 (.IMM(IR_q[31:0]), .IMM_SEL(MICROCODE_d_3), .OUT(imm_1_out));
  Counter #(.Bits(4)) counter_1 (.en(1'b1), .C(not_2_out), .clr(MICROCODE_d[24]), .out(counter_1_out));  // open: ovf
  _1_8_BIT_DUPLICATOR _1_8_bit_duplicator_1 (.IN(_4_to_1_or_1_out), .OUT(_1_8_bit_duplicator_1_out));
  Multiplexer #(.Bits(64)) multiplexer_6 (
    .sel(MICROCODE_d[8]), .in_0(reg_file_1_d_b), .in_1(imm_1_out), .out(multiplexer_6_out));
  Multiplexer #(.Bits(4)) multiplexer_7 (
    .sel(MICROCODE_d[7]), .in_0(IR_q[55:52]), .in_1(4'b1110), .out(multiplexer_7_out));
  assign and_2_out = IR_q[63:56] & _1_8_bit_duplicator_1_out;  // And and_2, 8 bits wide
  _4_TO_1_OR _4_to_1_or_1 (.IN(counter_1_out), .OUT(_4_to_1_or_1_out));
  ALU alu_1 (
    .A({reg_file_1_d_a_2, reg_file_1_d_a}), .B(multiplexer_6_out), .OP(MICROCODE_d_4), .C(alu_1_c),
    .OUT({alu_1_out_2, alu_1_out}), .Z(alu_1_z), .N(alu_1_n), .V(alu_1_v));
  REG_FILE reg_file_1 (
    .C(and_1_out), .D_in(multiplexer_4_out), .R_w(multiplexer_7_out), .R_a(IR_q[51:48]), .R_b(IR_q[47:44]),
    .we(MICROCODE_d[4]), .D_a({reg_file_1_d_a_2, reg_file_1_d_a}), .D_b(reg_file_1_d_b));
  ROM #(.AddrBits(12), .Bits(32)) MICROCODE (
    .A({and_2_out, counter_1_out}), .sel(1'b1),
    .D({MICROCODE_d[31:23], MICROCODE_d_6, MICROCODE_d[20], MICROCODE_d_5, MICROCODE_d[16:15], MICROCODE_d_4, MICROCODE_d_3, MICROCODE_d[8:7], MICROCODE_d_2, MICROCODE_d[4], MWR, MICROCODE_d[2:0]}));
  Register register_1 (.D(alu_1_c), .C(and_1_out), .en(MICROCODE_d[15]), .Q(register_1_q));
  Register register_2 (.D(alu_1_n), .C(and_1_out), .en(MICROCODE_d[15]), .Q(register_2_q));
  Register register_3 (.D(alu_1_v), .C(and_1_out), .en(MICROCODE_d[15]), .Q(register_3_q));
  Register register_4 (.D(alu_1_z), .C(and_1_out), .en(MICROCODE_d[15]), .Q(register_4_q));
  STORE_FORMATTER store_formatter_1 (
    .D_IN(reg_file_1_d_b), .LANE(MADDR[2:0]), .M_SIZE(MICROCODE_d_6), .M_OUT(MOUT), .M_BE(MBE));
  CONDITION_UNIT condition_unit_1 (
    .C(register_1_q), .N(register_2_q), .V(register_3_q), .Z(register_4_q), .COND(MICROCODE_d_5),
    .BRANCH(MICROCODE_d[16]), .JUMP(condition_unit_1_jump));

  // Notes on the sheet:
  //   contents of MICROCODE (hex, n*v repeats v):
  //   30100,400,15*0,405,15*0,40a,15*0,484,15*0,11,c24,14*0,11,c64,14*0
  //   ,600,15*0,1400,15*0,2400,15*0,100400,15*0,90,c24,14*0,90,c64,14*0
  //   ,200404,15*0,4040a,15*0,40405,15*0,8000,15*0,80408
endmodule

/* Test case TEST1:
CLK  RESET  MIN  DBGPC
C    1      0    0
C    0      0    8
C    0      0    8
C    0      0    16
C    0      0    16
C    0      0    24
*/

/* Test case TEST2:
CLK RESET MIN DBGPC DBG_STEP DBG_UC     DBG_PCEN DBG_CCLK
C   1     0   0     0        3          1        0
0   0     0   0     0        3          1        0
1   0     0   0     0        3          1        1
0   0     0   8     1        0x1000000  0        0
*/

/* Test case TEST3:
CLK RESET MIN                 DBGPC
C   1     0x1810000000000005  0
C   0     0x1810000000000005  8
C   0     0x1810000000000005  8
*/
