// Digital circuit IMM.dig as structural Verilog
module IMM (
  input  [31:0] IMM,
  input  [1:0] IMM_SEL,
  output [63:0] OUT
);

  Multiplexer #(.Bits(64), .Selector_Bits(2)) multiplexer_1 (
    .sel(IMM_SEL), .in_0({{33{IMM[31]}}, IMM[30:0]}), .in_1({{32{1'b0}}, IMM}), .in_2({IMM, {32{1'b0}}}),
    .in_3({64{1'b0}}), .out(OUT));
endmodule

/* Test case:
IMM          IMM_SEL  OUT

0x00000000   0        0x0000000000000000
0x00000005   0        0x0000000000000005
0x7FFFFFFF   0        0x000000007FFFFFFF
0x80000000   0        0xFFFFFFFF80000000
0xFFFFFFFF   0        0xFFFFFFFFFFFFFFFF
0xFFFFFFF8   0        0xFFFFFFFFFFFFFFF8
0xE0000000   0        0xFFFFFFFFE0000000
0x12345678   0        0x0000000012345678

0x00000000   1        0x0000000000000000
0x00000005   1        0x0000000000000005
0x7FFFFFFF   1        0x000000007FFFFFFF
0x80000000   1        0x0000000080000000
0xFFFFFFFF   1        0x00000000FFFFFFFF
0x12345678   1        0x0000000012345678

0x00000000   2        0x0000000000000000
0x00000001   2        0x0000000100000000
0x12345678   2        0x1234567800000000
0x80000000   2        0x8000000000000000
0xFFFFFFFF   2        0xFFFFFFFF00000000
*/
