// Digital circuit LOAD FORMATTER.dig as structural Verilog
module LOAD_FORMATTER (
  input  [63:0] M_IN,
  input  [2:0] LANE,
  input  [1:0] M_SIZE,
  input  M_SIGNED,
  output [63:0] OUT
);

  wire [7:0] _1_8_bit_duplicator_1_out;
  wire [15:0] _1_16_bit_duplicator_1_out;
  wire [31:0] _1_32_bit_duplicator_2_out;
  wire [63:0] barrelshifter_1_out;
  wire [63:8] barrelshifter_1_out_2;
  wire [63:32] _1_32_bit_duplicator_1_out;

  BarrelShifter #(.Bits(64), .direction("right")) barrelshifter_1 (
    .in(M_IN), .shift({1'b0, LANE, 3'b000}), .out({barrelshifter_1_out_2, barrelshifter_1_out[7:0]}));
  _1_32_BIT_DUPLICATOR _1_32_bit_duplicator_1 (.IN(barrelshifter_1_out_2[31]), .OUT(_1_32_bit_duplicator_1_out));
  _1_16_BIT_DUPLICATOR _1_16_bit_duplicator_1 (.IN(barrelshifter_1_out_2[15]), .OUT(_1_16_bit_duplicator_1_out));
  _1_32_BIT_DUPLICATOR _1_32_bit_duplicator_2 (.IN(barrelshifter_1_out_2[15]), .OUT(_1_32_bit_duplicator_2_out));
  _1_32_BIT_DUPLICATOR _1_32_bit_duplicator_3 (.IN(barrelshifter_1_out[7]), .OUT(barrelshifter_1_out[63:32]));
  _1_16_BIT_DUPLICATOR _1_16_bit_duplicator_2 (.IN(barrelshifter_1_out[7]), .OUT(barrelshifter_1_out[31:16]));
  _1_8_BIT_DUPLICATOR _1_8_bit_duplicator_1 (.IN(barrelshifter_1_out[7]), .OUT(_1_8_bit_duplicator_1_out));
  Multiplexer #(.Selector_Bits(3), .Bits(64)) multiplexer_1 (
    .sel({M_SIZE, M_SIGNED}), .in_0({{56{1'b0}}, barrelshifter_1_out[7:0]}),
    .in_1({barrelshifter_1_out[63:16], _1_8_bit_duplicator_1_out, barrelshifter_1_out[7:0]}),
    .in_2({{48{1'b0}}, barrelshifter_1_out_2[15:8], barrelshifter_1_out[7:0]}),
    .in_3({_1_32_bit_duplicator_2_out, _1_16_bit_duplicator_1_out, barrelshifter_1_out_2[15:8], barrelshifter_1_out[7:0]}),
    .in_4({{32{1'b0}}, barrelshifter_1_out_2[31:8], barrelshifter_1_out[7:0]}),
    .in_5({_1_32_bit_duplicator_1_out, barrelshifter_1_out_2[31:8], barrelshifter_1_out[7:0]}),
    .in_6({barrelshifter_1_out_2, barrelshifter_1_out[7:0]}),
    .in_7({barrelshifter_1_out_2, barrelshifter_1_out[7:0]}), .out(OUT));
endmodule

/* Test case:
M_IN                LANE  M_SIZE M_SIGNED OUT

0x0123456789ABCDEF  0     0      0        0x00000000000000EF
0x0123456789ABCDEF  0     0      1        0xFFFFFFFFFFFFFFEF
0x0123456789ABCDEF  1     0      0        0x00000000000000CD
0x0123456789ABCDEF  1     0      1        0xFFFFFFFFFFFFFFCD
0x0123456789ABCDEF  2     0      0        0x00000000000000AB
0x0123456789ABCDEF  2     0      1        0xFFFFFFFFFFFFFFAB
0x0123456789ABCDEF  3     0      0        0x0000000000000089
0x0123456789ABCDEF  3     0      1        0xFFFFFFFFFFFFFF89
0x0123456789ABCDEF  4     0      0        0x0000000000000067
0x0123456789ABCDEF  4     0      1        0x0000000000000067
0x0123456789ABCDEF  5     0      0        0x0000000000000045
0x0123456789ABCDEF  5     0      1        0x0000000000000045
0x0123456789ABCDEF  6     0      0        0x0000000000000023
0x0123456789ABCDEF  6     0      1        0x0000000000000023
0x0123456789ABCDEF  7     0      0        0x0000000000000001
0x0123456789ABCDEF  7     0      1        0x0000000000000001
0x0123456789ABCDEF  0     1      0        0x000000000000CDEF
0x0123456789ABCDEF  0     1      1        0xFFFFFFFFFFFFCDEF
0x0123456789ABCDEF  2     1      0        0x00000000000089AB
0x0123456789ABCDEF  2     1      1        0xFFFFFFFFFFFF89AB
0x0123456789ABCDEF  4     1      0        0x0000000000004567
0x0123456789ABCDEF  4     1      1        0x0000000000004567
0x0123456789ABCDEF  6     1      0        0x0000000000000123
0x0123456789ABCDEF  6     1      1        0x0000000000000123
0x0123456789ABCDEF  0     2      0        0x0000000089ABCDEF
0x0123456789ABCDEF  0     2      1        0xFFFFFFFF89ABCDEF
0x0123456789ABCDEF  4     2      0        0x0000000001234567
0x0123456789ABCDEF  4     2      1        0x0000000001234567
0x0123456789ABCDEF  0     3      0        0x0123456789ABCDEF
0x0123456789ABCDEF  0     3      1        0x0123456789ABCDEF

0x80FF7F017FFF8000  0     0      0        0x0000000000000000
0x80FF7F017FFF8000  0     0      1        0x0000000000000000
0x80FF7F017FFF8000  1     0      0        0x0000000000000080
0x80FF7F017FFF8000  1     0      1        0xFFFFFFFFFFFFFF80
0x80FF7F017FFF8000  2     0      0        0x00000000000000FF
0x80FF7F017FFF8000  2     0      1        0xFFFFFFFFFFFFFFFF
0x80FF7F017FFF8000  3     0      0        0x000000000000007F
0x80FF7F017FFF8000  3     0      1        0x000000000000007F
0x80FF7F017FFF8000  4     0      0        0x0000000000000001
0x80FF7F017FFF8000  4     0      1        0x0000000000000001
0x80FF7F017FFF8000  5     0      0        0x000000000000007F
0x80FF7F017FFF8000  5     0      1        0x000000000000007F
0x80FF7F017FFF8000  6     0      0        0x00000000000000FF
0x80FF7F017FFF8000  6     0      1        0xFFFFFFFFFFFFFFFF
0x80FF7F017FFF8000  7     0      0        0x0000000000000080
0x80FF7F017FFF8000  7     0      1        0xFFFFFFFFFFFFFF80
0x80FF7F017FFF8000  0     1      0        0x0000000000008000
0x80FF7F017FFF8000  0     1      1        0xFFFFFFFFFFFF8000
0x80FF7F017FFF8000  2     1      0        0x0000000000007FFF
0x80FF7F017FFF8000  2     1      1        0x0000000000007FFF
0x80FF7F017FFF8000  4     1      0        0x0000000000007F01
0x80FF7F017FFF8000  4     1      1        0x0000000000007F01
0x80FF7F017FFF8000  6     1      0        0x00000000000080FF
0x80FF7F017FFF8000  6     1      1        0xFFFFFFFFFFFF80FF
0x80FF7F017FFF8000  0     2      0        0x000000007FFF8000
0x80FF7F017FFF8000  0     2      1        0x000000007FFF8000
0x80FF7F017FFF8000  4     2      0        0x0000000080FF7F01
0x80FF7F017FFF8000  4     2      1        0xFFFFFFFF80FF7F01
0x80FF7F017FFF8000  0     3      0        0x80FF7F017FFF8000
0x80FF7F017FFF8000  0     3      1        0x80FF7F017FFF8000
*/
