// Digital circuit MB.dig as structural Verilog
module MB (
  input  CLK,
  input  RESET,
  input  [63:0] X0,
  input  [63:0] X1,
  input  [63:0] X2,
  input  [63:0] X3,
  output [63:0] DISPLAY
);

  wire and_1_out, CART__SEL_eq, cpu_1_p4, DISP_eq, IO__SEL_eq, RAM__SEL_eq;
  wire [1:0] cpu_1_p7_2, or_1_out;
  wire [7:0] cpu_1_p5;
  wire [31:0] cpu_1_p7;
  wire [63:0] BOOT_d, CARTIRAGE_d, cpu_1_p6, mem64_1_dout, multiplexer_1_out, multiplexer_2_out;

  Multiplexer #(.Bits(64), .Selector_Bits(2)) multiplexer_1 (
    .sel(cpu_1_p7_2), .in_0(X0), .in_1(X1), .in_2(X2), .in_3(X3), .out(multiplexer_1_out));
  ROM #(.bigEndian("true"), .AddrBits(13), .Bits(64)) BOOT (.A({cpu_1_p7[15:5], cpu_1_p7_2}), .sel(1'b1), .D(BOOT_d));
  ROM #(.bigEndian("true"), .AddrBits(13), .Bits(64)) CARTIRAGE (
    .A({cpu_1_p7[15:5], cpu_1_p7_2}), .sel(1'b1), .D(CARTIRAGE_d));
  Multiplexer #(.Bits(64), .Selector_Bits(2)) multiplexer_2 (
    .sel(or_1_out), .in_0(BOOT_d), .in_1(mem64_1_dout), .in_2(CARTIRAGE_d), .in_3(multiplexer_1_out),
    .out(multiplexer_2_out));
  // CPU cpu_1: pin names not known; wires that end beside it: RESET, multiplexer_2_out, CLK, cpu_1_p4, cpu_1_p5, cpu_1_p6, {cpu_1_p7[31:5], cpu_1_p7_2, cpu_1_p7[2:0]}
  Comparator #(.Bits(12)) BOOT__SEL (.a(cpu_1_p7[31:20]), .b({12{1'b0}}));  // open: gt, eq, lt
  Comparator #(.Bits(12)) RAM__SEL (.a(cpu_1_p7[31:20]), .b(12'h1), .eq(RAM__SEL_eq));  // open: gt, lt
  Comparator #(.Bits(12)) CART__SEL (.a(cpu_1_p7[31:20]), .b(12'he00), .eq(CART__SEL_eq));  // open: gt, lt
  Comparator #(.Bits(12)) IO__SEL (.a(cpu_1_p7[31:20]), .b(12'hf00), .eq(IO__SEL_eq));  // open: gt, lt
  or or_1 (or_1_out[0], RAM__SEL_eq, IO__SEL_eq);
  or or_2 (or_1_out[1], CART__SEL_eq, IO__SEL_eq);
  MEM64 mem64_1 (
    .A({cpu_1_p7[19:5], cpu_1_p7_2}), .DIN(cpu_1_p6), .MBE(cpu_1_p5), .WE(cpu_1_p4), .CS(RAM__SEL_eq),
    .CLK(CLK), .DOUT(mem64_1_dout));
  Comparator #(.Bits(32)) DISP (
    .a({cpu_1_p7[31:5], cpu_1_p7_2, cpu_1_p7[2:0]}), .b(32'hf0000100), .eq(DISP_eq));  // open: gt, lt
  and and_1 (and_1_out, DISP_eq, cpu_1_p4);
  Register #(.Bits(64)) DISP__REG (.D(cpu_1_p6), .C(CLK), .en(and_1_out), .Q(DISPLAY));

  // Notes on the sheet:
  //   CLK: Hz: 1000
  //   BOOT loads boot.bin
  //   CARTIRAGE loads cart.bin
endmodule

/* Test case CALC1:
CLK RESET X0 X1 X2 X3 DISPLAY
C   1     7  5  0  0  X
repeat(600) C 0 7 5 0 0 X
0   0     7  5  0  0  12
*/

/* Test case CALC2:
CLK RESET X0 X1 X2 X3 DISPLAY
C   1     7  5  1  0  X
repeat(600) C 0 7 5 1 0 X
0   0     7  5  1  0  2
*/

/* Test case CALC3:
CLK RESET X0 X1 X2 X3 DISPLAY
C   1     7  5  2  0  X
repeat(600) C 0 7 5 2 0 X
0   0     7  5  2  0  35
*/
