// Digital circuit MEM64.dig as structural Verilog
module MEM64 (
  input  [16:0] A,
  input  [63:0] DIN,
  input  [7:0] MBE,
  input  WE,
  input  CS,
  input  CLK,
  output [63:0] DOUT
);

  wire and_1_out, and_2_out, and_3_out, and_4_out, and_5_out, and_6_out, and_7_out, and_8_out;

  and and_1 (and_1_out, MBE[0], WE, CS);
  and and_2 (and_2_out, MBE[1], WE, CS);
  and and_3 (and_3_out, MBE[2], WE, CS);
  and and_4 (and_4_out, MBE[3], WE, CS);
  and and_5 (and_5_out, MBE[4], WE, CS);
  and and_6 (and_6_out, MBE[5], WE, CS);
  and and_7 (and_7_out, MBE[6], WE, CS);
  and and_8 (and_8_out, MBE[7], WE, CS);
  RAMDualPort #(.AddrBits(17), .Bits(8)) ramdualport_1 (
    .A(A), .Din(DIN[7:0]), .str(and_1_out), .C(CLK), .ld(1'b1), .D(DOUT[7:0]));
  RAMDualPort #(.AddrBits(17), .Bits(8)) ramdualport_2 (
    .A(A), .Din(DIN[39:32]), .str(and_5_out), .C(CLK), .ld(1'b1), .D(DOUT[39:32]));
  RAMDualPort #(.AddrBits(17), .Bits(8)) ramdualport_3 (
    .A(A), .Din(DIN[15:8]), .str(and_2_out), .C(CLK), .ld(1'b1), .D(DOUT[15:8]));
  RAMDualPort #(.AddrBits(17), .Bits(8)) ramdualport_4 (
    .A(A), .Din(DIN[47:40]), .str(and_6_out), .C(CLK), .ld(1'b1), .D(DOUT[47:40]));
  RAMDualPort #(.AddrBits(17), .Bits(8)) ramdualport_5 (
    .A(A), .Din(DIN[23:16]), .str(and_3_out), .C(CLK), .ld(1'b1), .D(DOUT[23:16]));
  RAMDualPort #(.AddrBits(17), .Bits(8)) ramdualport_6 (
    .A(A), .Din(DIN[55:48]), .str(and_7_out), .C(CLK), .ld(1'b1), .D(DOUT[55:48]));
  RAMDualPort #(.AddrBits(17), .Bits(8)) ramdualport_7 (
    .A(A), .Din(DIN[31:24]), .str(and_4_out), .C(CLK), .ld(1'b1), .D(DOUT[31:24]));
  RAMDualPort #(.AddrBits(17), .Bits(8)) ramdualport_8 (
    .A(A), .Din(DIN[63:56]), .str(and_8_out), .C(CLK), .ld(1'b1), .D(DOUT[63:56]));
endmodule

/* Test case:
A        DIN                  MBE   WE  CS  CLK  DOUT
0        0x0123456789ABCDEF   0xFF  1   1   C    0x0123456789ABCDEF
0        0                    0     0   1   0    0x0123456789ABCDEF
0        0x0000000041000000   0x08  1   1   C    0x0123456741ABCDEF
0        0x7777000000000000   0xC0  1   1   C    0x7777456741ABCDEF
0        0                    0xFF  0   1   C    0x7777456741ABCDEF
0        0                    0xFF  1   0   C    0x7777456741ABCDEF
1        0xFFFFFFFFFFFFFFFF   0xFF  1   1   C    0xFFFFFFFFFFFFFFFF
0        0                    0     0   1   0    0x7777456741ABCDEF
0x1FFFF  0x1122334455667788   0xFF  1   1   C    0x1122334455667788
0x1FFFF  0x00000000000000AA   0x01  1   1   C    0x11223344556677AA
1        0                    0     0   1   0    0xFFFFFFFFFFFFFFFF
0        0x5555555555555555   0x01  1   1   C    0x7777456741ABCD55
0        0x5555555555555555   0x80  1   1   C    0x5577456741ABCD55
*/
