// Digital circuit PG CHIP.dig as structural Verilog
module PG_CHIP (
  input  A,
  input  B,
  output G,
  output P
);

  and and_1 (G, B, A);
  xor xor_1 (P, B, A);
endmodule

/* Test case:
A  B  G  P
0  0  0  0
0  1  0  1
1  0  0  1
1  1  1  0
*/
