// Digital circuit REG FILE.dig as structural Verilog
module REG_FILE (
  input  C,
  input  [63:0] D_in,
  input  [3:0] R_w,
  input  [3:0] R_a,
  input  [3:0] R_b,
  input  we,
  output [63:0] D_a,
  output [63:0] D_b
);

  wire and_1_out, and_2_out, and_3_out, and_4_out, and_5_out, and_6_out, and_7_out, and_8_out, and_9_out,
       and_10_out, and_11_out, and_12_out, and_13_out, and_14_out, and_15_out, decoder_1_out_1,
       decoder_1_out_2, decoder_1_out_3, decoder_1_out_4, decoder_1_out_5, decoder_1_out_6, decoder_1_out_7,
       decoder_1_out_8, decoder_1_out_9, decoder_1_out_10, decoder_1_out_11, decoder_1_out_12,
       decoder_1_out_13, decoder_1_out_14, decoder_1_out_15;
  wire [63:0] R1_q, R2_q, R3_q, R4, R5, R6, R7_q, R8, R9, R10, R11_q, R12, R13, R14, R15_q;

  Decoder #(.Selector_Bits(4)) decoder_1 (
    .sel(R_w), .out_1(decoder_1_out_1), .out_2(decoder_1_out_2), .out_3(decoder_1_out_3),
    .out_4(decoder_1_out_4), .out_5(decoder_1_out_5), .out_6(decoder_1_out_6), .out_7(decoder_1_out_7),
    .out_8(decoder_1_out_8), .out_9(decoder_1_out_9), .out_10(decoder_1_out_10), .out_11(decoder_1_out_11),
    .out_12(decoder_1_out_12), .out_13(decoder_1_out_13), .out_14(decoder_1_out_14), .out_15(decoder_1_out_15));  // open: out_0
  and and_1 (and_1_out, we, decoder_1_out_1);
  and and_2 (and_2_out, we, decoder_1_out_2);
  and and_3 (and_3_out, we, decoder_1_out_3);
  and and_4 (and_4_out, we, decoder_1_out_4);
  and and_5 (and_5_out, we, decoder_1_out_5);
  and and_6 (and_6_out, we, decoder_1_out_6);
  and and_7 (and_7_out, we, decoder_1_out_7);
  and and_8 (and_8_out, we, decoder_1_out_8);
  and and_9 (and_9_out, we, decoder_1_out_9);
  and and_10 (and_10_out, we, decoder_1_out_10);
  and and_11 (and_11_out, we, decoder_1_out_11);
  and and_12 (and_12_out, we, decoder_1_out_12);
  and and_13 (and_13_out, we, decoder_1_out_13);
  and and_14 (and_14_out, we, decoder_1_out_14);
  and and_15 (and_15_out, we, decoder_1_out_15);
  Register #(.Bits(64)) u_R4 (.D(D_in), .C(C), .en(and_4_out), .Q(R4));
  Register #(.Bits(64)) u_R8 (.D(D_in), .C(C), .en(and_8_out), .Q(R8));
  Register #(.Bits(64)) u_R12 (.D(D_in), .C(C), .en(and_12_out), .Q(R12));
  Register #(.Bits(64)) R1 (.D(D_in), .C(C), .en(and_1_out), .Q(R1_q));
  Register #(.Bits(64)) u_R5 (.D(D_in), .C(C), .en(and_5_out), .Q(R5));
  Register #(.Bits(64)) u_R9 (.D(D_in), .C(C), .en(and_9_out), .Q(R9));
  Register #(.Bits(64)) u_R13 (.D(D_in), .C(C), .en(and_13_out), .Q(R13));
  Register #(.Bits(64)) R2 (.D(D_in), .C(C), .en(and_2_out), .Q(R2_q));
  Register #(.Bits(64)) u_R6 (.D(D_in), .C(C), .en(and_6_out), .Q(R6));
  Register #(.Bits(64)) u_R10 (.D(D_in), .C(C), .en(and_10_out), .Q(R10));
  Register #(.Bits(64)) u_R14 (.D(D_in), .C(C), .en(and_14_out), .Q(R14));
  Register #(.Bits(64)) R3 (.D(D_in), .C(C), .en(and_3_out), .Q(R3_q));
  Register #(.Bits(64)) R7 (.D(D_in), .C(C), .en(and_7_out), .Q(R7_q));
  Register #(.Bits(64)) R11 (.D(D_in), .C(C), .en(and_11_out), .Q(R11_q));
  Register #(.Bits(64)) R15 (.D(D_in), .C(C), .en(and_15_out), .Q(R15_q));
  Multiplexer #(.Selector_Bits(4), .Bits(64)) multiplexer_1 (
    .sel(R_a), .in_0({64{1'b0}}), .in_1(R1_q), .in_2(R2_q), .in_3(R3_q), .in_4(R4), .in_5(R5), .in_6(R6),
    .in_7(R7_q), .in_8(R8), .in_9(R9), .in_10(R10), .in_11(R11_q), .in_12(R12), .in_13(R13), .in_14(R14),
    .in_15(R15_q), .out(D_a));
  Multiplexer #(.Selector_Bits(4), .Bits(64)) multiplexer_2 (
    .sel(R_b), .in_0({64{1'b0}}), .in_1(R1_q), .in_2(R2_q), .in_3(R3_q), .in_4(R4), .in_5(R5), .in_6(R6),
    .in_7(R7_q), .in_8(R8), .in_9(R9), .in_10(R10), .in_11(R11_q), .in_12(R12), .in_13(R13), .in_14(R14),
    .in_15(R15_q), .out(D_b));
endmodule

/* Test case:
R_a  R_b  R_w     D_in                          we  C   D_a                           D_b

# 1. write R1..R15 with different values (R0 must read 0 the whole time)
loop(i,15)
0   0   (i+1)  ((i+1)*0x0101010101010101)   1   C   0                            0
end loop

# 2. read them all back, two ports at once, different registers on each
loop(i,15)
(i+1)  (15-i)  0   0                        0   0   ((i+1)*0x0101010101010101)   ((15-i)*0x0101010101010101)
end loop

# 3. both ports reading the same register
5   5   0   0                               0   0   0x0505050505050505           0x0505050505050505

# 4. we = 0 must not write
0   0   3   0xDEADBEEFDEADBEEF              0   C   0                            0
3   3   0   0                               0   0   0x0303030303030303           0x0303030303030303

# 5. writing R0 is ignored
0   0   0   0x123456789ABCDEF0              1   C   0                            0
0   0   0   0                               0   0   0                            0

# 6. overwrite with the top and bottom bits set, neighbours untouched
0   0   15  0x8000000000000001              1   C   0                            0
15  14  0   0                               0   0   0x8000000000000001           0x0E0E0E0E0E0E0E0E
1   15  0   0                               0   0   0x0101010101010101           0x8000000000000001

# 7. all ones and all zeros
0   0   7   0xFFFFFFFFFFFFFFFF              1   C   0                            0
0   0   8   0                               1   C   0                            0
7   8   0   0                               0   0   0xFFFFFFFFFFFFFFFF           0
*/
