// Digital circuit STORE FORMATTER.dig as structural Verilog
module STORE_FORMATTER (
  input  [63:0] D_IN,
  input  [2:0] LANE,
  input  [1:0] M_SIZE,
  output [63:0] M_OUT,
  output [7:0] M_BE
);

  wire [7:0] multiplexer_1_out;

  BarrelShifter #(.Bits(64)) barrelshifter_1 (.in(D_IN), .shift({1'b0, LANE, 3'b000}), .out(M_OUT));
  Multiplexer #(.Bits(8), .Selector_Bits(2)) multiplexer_1 (
    .sel(M_SIZE), .in_0(8'h1), .in_1(8'h3), .in_2(8'hf), .in_3({8{1'b1}}), .out(multiplexer_1_out));
  BarrelShifter #(.Bits(8)) barrelshifter_2 (.in(multiplexer_1_out), .shift({1'b0, LANE}), .out(M_BE));
endmodule

/* Test case:
D_IN                LANE  M_SIZE  M_OUT                M_BE

0x0123456789ABCDEF  0     0      0x0123456789ABCDEF  0x01
0x0123456789ABCDEF  1     0      0x23456789ABCDEF00  0x02
0x0123456789ABCDEF  2     0      0x456789ABCDEF0000  0x04
0x0123456789ABCDEF  3     0      0x6789ABCDEF000000  0x08
0x0123456789ABCDEF  4     0      0x89ABCDEF00000000  0x10
0x0123456789ABCDEF  5     0      0xABCDEF0000000000  0x20
0x0123456789ABCDEF  6     0      0xCDEF000000000000  0x40
0x0123456789ABCDEF  7     0      0xEF00000000000000  0x80
0x0123456789ABCDEF  0     1      0x0123456789ABCDEF  0x03
0x0123456789ABCDEF  2     1      0x456789ABCDEF0000  0x0C
0x0123456789ABCDEF  4     1      0x89ABCDEF00000000  0x30
0x0123456789ABCDEF  6     1      0xCDEF000000000000  0xC0
0x0123456789ABCDEF  0     2      0x0123456789ABCDEF  0x0F
0x0123456789ABCDEF  4     2      0x89ABCDEF00000000  0xF0
0x0123456789ABCDEF  0     3      0x0123456789ABCDEF  0xFF

0xFFFFFFFFFFFFFF41  0     0      0xFFFFFFFFFFFFFF41  0x01
0xFFFFFFFFFFFFFF41  1     0      0xFFFFFFFFFFFF4100  0x02
0xFFFFFFFFFFFFFF41  2     0      0xFFFFFFFFFF410000  0x04
0xFFFFFFFFFFFFFF41  3     0      0xFFFFFFFF41000000  0x08
0xFFFFFFFFFFFFFF41  4     0      0xFFFFFF4100000000  0x10
0xFFFFFFFFFFFFFF41  5     0      0xFFFF410000000000  0x20
0xFFFFFFFFFFFFFF41  6     0      0xFF41000000000000  0x40
0xFFFFFFFFFFFFFF41  7     0      0x4100000000000000  0x80
0xFFFFFFFFFFFFFF41  0     1      0xFFFFFFFFFFFFFF41  0x03
0xFFFFFFFFFFFFFF41  2     1      0xFFFFFFFFFF410000  0x0C
0xFFFFFFFFFFFFFF41  4     1      0xFFFFFF4100000000  0x30
0xFFFFFFFFFFFFFF41  6     1      0xFF41000000000000  0xC0
0xFFFFFFFFFFFFFF41  0     2      0xFFFFFFFFFFFFFF41  0x0F
0xFFFFFFFFFFFFFF41  4     2      0xFFFFFF4100000000  0xF0
0xFFFFFFFFFFFFFF41  0     3      0xFFFFFFFFFFFFFF41  0xFF
*/
