// Digital circuit TB.dig as structural Verilog
module TB (
  input  RESET,
  input  CLK,
  output [31:0] DBG_PC
);

  wire comparator_1_eq, cpu_1_p4;
  wire [7:0] cpu_1_p5;
  wire [16:0] cpu_1_p8_2;
  wire [31:0] cpu_1_p8;
  wire [63:0] cpu_1_p6, mem64_1_dout, multiplexer_1_out, rom_1_d;

  ROM #(.bigEndian("true"), .AddrBits(13), .Bits(64)) rom_1 (.A(cpu_1_p8_2[12:0]), .sel(1'b1), .D(rom_1_d));
  Multiplexer #(.Bits(64)) multiplexer_1 (
    .sel(comparator_1_eq), .in_0(rom_1_d), .in_1(mem64_1_dout), .out(multiplexer_1_out));
  // CPU cpu_1: pin names not known; wires that end beside it: RESET, multiplexer_1_out, CLK, cpu_1_p4, cpu_1_p5, cpu_1_p6, DBG_PC, {cpu_1_p8[31:20], cpu_1_p8_2, cpu_1_p8[2:0]}
  Comparator #(.Bits(12)) comparator_1 (.a(cpu_1_p8[31:20]), .b(12'h1), .eq(comparator_1_eq));  // open: gt, lt
  MEM64 mem64_1 (
    .A(cpu_1_p8_2), .DIN(cpu_1_p6), .MBE(cpu_1_p5), .WE(cpu_1_p4), .CS(comparator_1_eq), .CLK(CLK),
    .DOUT(mem64_1_dout));

  // Notes on the sheet:
  //   rom_1 loads test2.bin
endmodule

/* Test case TEST1:
CLK  RESET  DBG_PC
C    1      X
repeat(200) C 0 X
0    0      0x1E8
*/

/* Test case TEST2:
CLK  RESET  DBG_PC
C    1      X
repeat(500) C 0 X
0    0      0x170
*/
