// Digital circuit TB_000.dig as structural Verilog
module TB_000 (
  input  RESET,
  input  CLK,
  output [31:0] DBG_PC
);

  wire and_1_out, and_2_out, and_3_out, and_4_out, and_5_out, and_6_out, and_7_out, and_8_out,
       comparator_1_eq, cpu_1_p4;
  wire [7:0] cpu_1_p5, cpu_1_p6, cpu_1_p6_2, cpu_1_p6_3, cpu_1_p6_4, cpu_1_p6_5, cpu_1_p6_6, cpu_1_p6_7,
       cpu_1_p6_8, ramdualport_1_d, ramdualport_2_d, ramdualport_3_d, ramdualport_4_d, ramdualport_5_d;
  wire [16:0] cpu_1_p8_2;
  wire [31:0] cpu_1_p8;
  wire [63:0] multiplexer_1_out, rom_1_d;
  wire [63:40] ramdualport_6_d;

  ROM #(.bigEndian("true"), .AddrBits(13), .Bits(64)) rom_1 (.A(cpu_1_p8_2[12:0]), .sel(1'b1), .D(rom_1_d));
  Multiplexer #(.Bits(64)) multiplexer_1 (
    .sel(comparator_1_eq), .in_0(rom_1_d),
    .in_1({ramdualport_6_d, ramdualport_5_d, ramdualport_4_d, ramdualport_3_d, ramdualport_2_d, ramdualport_1_d}),
    .out(multiplexer_1_out));
  // CPU cpu_1: pin names not known; wires that end beside it: RESET, multiplexer_1_out, CLK, cpu_1_p4, cpu_1_p5, {cpu_1_p6_8, cpu_1_p6_7, cpu_1_p6_6, cpu_1_p6_5, cpu_1_p6_4, cpu_1_p6_3, cpu_1_p6_2, cpu_1_p6}, DBG_PC, {cpu_1_p8[31:20], cpu_1_p8_2, cpu_1_p8[2:0]}
  Comparator #(.Bits(12)) comparator_1 (.a(cpu_1_p8[31:20]), .b(12'h1), .eq(comparator_1_eq));  // open: gt, lt
  and and_1 (and_1_out, cpu_1_p5[0], comparator_1_eq, cpu_1_p4);
  RAMDualPort #(.AddrBits(17), .Bits(8)) ramdualport_1 (
    .A(cpu_1_p8_2), .Din(cpu_1_p6), .str(and_1_out), .C(CLK), .ld(1'b1), .D(ramdualport_1_d));
  and and_2 (and_2_out, cpu_1_p5[1], comparator_1_eq, cpu_1_p4);
  RAMDualPort #(.AddrBits(17), .Bits(8)) ramdualport_2 (
    .A(cpu_1_p8_2), .Din(cpu_1_p6_2), .str(and_2_out), .C(CLK), .ld(1'b1), .D(ramdualport_2_d));
  and and_3 (and_3_out, cpu_1_p5[2], comparator_1_eq, cpu_1_p4);
  RAMDualPort #(.AddrBits(17), .Bits(8)) ramdualport_3 (
    .A(cpu_1_p8_2), .Din(cpu_1_p6_3), .str(and_3_out), .C(CLK), .ld(1'b1), .D(ramdualport_3_d));
  and and_4 (and_4_out, cpu_1_p5[3], comparator_1_eq, cpu_1_p4);
  RAMDualPort #(.AddrBits(17), .Bits(8)) ramdualport_4 (
    .A(cpu_1_p8_2), .Din(cpu_1_p6_4), .str(and_4_out), .C(CLK), .ld(1'b1), .D(ramdualport_4_d));
  and and_5 (and_5_out, cpu_1_p5[4], comparator_1_eq, cpu_1_p4);
  RAMDualPort #(.AddrBits(17), .Bits(8)) ramdualport_5 (
    .A(cpu_1_p8_2), .Din(cpu_1_p6_5), .str(and_5_out), .C(CLK), .ld(1'b1), .D(ramdualport_5_d));
  and and_6 (and_6_out, cpu_1_p5[5], comparator_1_eq, cpu_1_p4);
  RAMDualPort #(.AddrBits(17), .Bits(8)) ramdualport_6 (
    .A(cpu_1_p8_2), .Din(cpu_1_p6_6), .str(and_6_out), .C(CLK), .ld(1'b1), .D(ramdualport_6_d[47:40]));
  and and_7 (and_7_out, cpu_1_p5[6], comparator_1_eq, cpu_1_p4);
  RAMDualPort #(.AddrBits(17), .Bits(8)) ramdualport_7 (
    .A(cpu_1_p8_2), .Din(cpu_1_p6_7), .str(and_7_out), .C(CLK), .ld(1'b1), .D(ramdualport_6_d[55:48]));
  and and_8 (and_8_out, cpu_1_p5[7], comparator_1_eq, cpu_1_p4);
  RAMDualPort #(.AddrBits(17), .Bits(8)) ramdualport_8 (
    .A(cpu_1_p8_2), .Din(cpu_1_p6_8), .str(and_8_out), .C(CLK), .ld(1'b1), .D(ramdualport_6_d[63:56]));

  // Notes on the sheet:
  //   rom_1 loads test2.bin
endmodule

/* Test case TEST1:
CLK  RESET  DBG_PC
C    1      X
repeat(200) C 0 X
0    0      0x1E8
*/

/* Test case TEST2:
CLK  RESET  DBG_PC
C    1      X
repeat(500) C 0 X
0    0      0x170
*/
